# Fritzing sketch RaspberryPi_DHT11 (saved by Fritzing 0.9.3b)
breadboards: 1

parts:
  Raspberry_Pi_1 = Raspberry Pi 3 [part_number=RPI-3-V1.2]
  DHT1 = Humidity and Temperature Sensor DHT11
  R1 = Resistor [tolerance=±5% resistance=10k package="0805 [SMD]"]

nets:
  N1: Raspberry_Pi_1.GPIO4, DHT1.Data-signal, R1.Pin_0
  N2: Raspberry_Pi_1.GND, DHT1.GND_2
  5V: Raspberry_Pi_1.5V, DHT1.Vcc, R1.Pin_1

custom parts:
  Humidity and Temperature Sensor DHT11: Digital relative humidity & temperature sensor DHT11
